# Fritzing sketch auto-backlight-circuit (saved by Fritzing 0.9.3b)
breadboards: 1

parts:
  2N3904 = TRANSISTOR_NPN [package=to-92-ammo]
  LED1 = smd LED [color="White (8000K)" package="1206 [SMD]"]
  R3 = Photocell (LDR) [package=THT]
  VCC1 = 4 x AAA Battery Mount
  R1 = Resistor [tolerance=±5% resistance=1k package=THT]
  R2 = Resistor [tolerance=±5% resistance=22 package=THT]

nets:
  N1: 2N3904.E, R2.Pin_0
  N2: 2N3904.B, R3.pin_0, R1.Pin_1
  N3: 2N3904.C, VCC1.+, R1.Pin_0
  N4: LED1.cathode, R3.pin_1, VCC1.-
  N5: LED1.anode, R2.Pin_1
