# Fritzing sketch latching-circuit (saved by Fritzing 0.9.3b)

parts:
  WeMos_D1_Mini1 = WeMos D1 Mini
  U1 = LIPO-1000mAh [package=lipo-1000]
  Q1 = MOSFET-NCHANNEL [package=to-92]
  S1 = SWITCH-MOMENTARY-2 [package=tactile-pth-12mm]
  R2 = Resistor [tolerance=±5% resistance=10k package=THT]
  R1 = Resistor [tolerance=±5% resistance=10k package=THT]
  Q2 = Basic FET P-Channel [package="TO220 [THT]"]

nets:
  N1: WeMos_D1_Mini1.5V, S1.2, Q2.source
  N2: WeMos_D1_Mini1.D0, Q1.G, R1.Pin_0
  N3: WeMos_D1_Mini1.G, U1.-, Q1.S, R1.Pin_1
  N4: U1.+, S1.1, R2.Pin_0, Q2.drain
  N5: Q1.D, R2.Pin_1, Q2.gate
