# Fritzing sketch nokia 5110 (saved by Fritzing 0.7.9b)
breadboards: 1

parts:
  Arduino1 = Arduino
  Nokia_5110_LCD_Module1 = Nokia5110LCDModule
  part = Zener Diode [part_number=1N4732A breakdown_voltage=3.6V package="300 mil [THT]"]  # not connected
  part_2 = 1k Ω Resistor [package=THT]  # not connected
  part_3 = Rectifier Diode  # not connected
  part_4 = Rectifier Diode  # not connected
  part_5 = 100 Ω Resistor [package=THT]  # not connected
  R1 = 47 Ω Resistor [package=THT]
  R2 = 47 Ω Resistor [package=THT]
  D1 = Rectifier Diode
  D2 = Rectifier Diode
  R3 = Trimmer Potentiometer [package=THT]
  R4 = 1k Ω Resistor [package=THT]

nets:
  N1: Arduino1.D7, Nokia_5110_LCD_Module1.Grnd
  N2: Arduino1.D6, Nokia_5110_LCD_Module1.Vcc
  N3: Arduino1.D5, Nokia_5110_LCD_Module1.SCE
  N4: Arduino1.D4, R2.Pin_1
  N5: Arduino1.D3, R1.Pin_1
  N6: Arduino1.+5V, R3.leg1, R4.Pin_1
  N7: Arduino1.GND, Nokia_5110_LCD_Module1.LED, D1.anode, D2.anode, R3.leg2
  N8: Nokia_5110_LCD_Module1.RST, R2.Pin_0, D2.cathode
  N9: Nokia_5110_LCD_Module1.D/C, R1.Pin_0, D1.cathode
  N10: Nokia_5110_LCD_Module1.6_DN_(MOSI), R3.wiper
  N11: Nokia_5110_LCD_Module1.SCLK, R4.Pin_0

custom parts:
  : Nokia 5110 LCD with 8 pin. It's a 45mm*45mm module part. Description: The Nokia 5110 is a basic graphic LCD screen for lots of applications. It was originally intended for as a cell phone screen. This one is mounted on an easy to solder PCB. It uses the PCD8544 controller. The PCD8544 is a low power CMOS LCD controller/driver, designed to drive a graphic display of 48 rows and 84 columns. All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
  Rectifier Diode: Ageneral purpose zener diode
