# Fritzing sketch simplified-circuit (saved by Fritzing 0.9.3b)
breadboards: 1

parts:
  WeMos_D1_Mini1 = WeMos D1 Mini
  Part1 = HX711 Weighing Sensor Module
  C2 = Electrolytic Capacitor [capacitance=47µF voltage=16V package="0405 [SMD, electrolytic]"]
  C1 = Ceramic Capacitor [capacitance="100 nF" voltage=10V package="200 mil [THT, multilayer]"]
  C3 = Ceramic Capacitor [capacitance="100 nF" voltage=10V package="200 mil [THT, multilayer]"]
  C4 = Ceramic Capacitor [capacitance=10nF voltage=10V package="200 mil [THT, multilayer]"]
  Load_Cell1 = Load Cell - Red/white/black/green
  Nokia_5110_LCD_Module1 = Nokia5110LCDModule
  R1 = Resistor [tolerance=±5% resistance=10k package=THT]
  R2 = Resistor [tolerance=±5% resistance=220k package=THT]
  BAT1 = LIPO-1000mAh [package=lipo-1000]
  R3 = Resistor [tolerance=±5% resistance=22 package=THT]
  LED2 = LED - 3mm [color="White (8000K)" package="3 mm [THT]"]
  S1 = Pushbutton [package="[THT]"]
  R4 = Resistor [tolerance=±5% resistance=10k package=THT]

nets:
  VCC: WeMos_D1_Mini1.3V3, Part1.VCC, C3.1, C4.1, Nokia_5110_LCD_Module1.Vcc, Nokia_5110_LCD_Module1.LED, LED2.cathode, S1.Pin_1, S1.Pin_2
  N1: WeMos_D1_Mini1.5V, C2.+, C1.1, R2.Pin_1, BAT1.+
  N2: WeMos_D1_Mini1.A0, R2.Pin_0
  N3: WeMos_D1_Mini1.D1, Part1.DO/RX
  N4: WeMos_D1_Mini1.D2, Part1.CK/TX
  N5: WeMos_D1_Mini1.D3, R3.Pin_0
  N6: WeMos_D1_Mini1.D5, Nokia_5110_LCD_Module1.SCLK
  N7: WeMos_D1_Mini1.D6, Nokia_5110_LCD_Module1.D/C
  N8: WeMos_D1_Mini1.D7, Nokia_5110_LCD_Module1.6_DN_(MOSI)
  N9: WeMos_D1_Mini1.D8, S1.Pin_3, S1.Pin_4, R4.Pin_1
  N10: WeMos_D1_Mini1.G, Part1.GND, C2.-, C1.0, C3.0, C4.0, Nokia_5110_LCD_Module1.Grnd, Nokia_5110_LCD_Module1.SCE, BAT1.-, R4.Pin_0
  N11: WeMos_D1_Mini1.RST, R1.Pin_1
  N12: Part1.E+, Load_Cell1.wire1
  N13: Part1.E-, Load_Cell1.wire3
  N14: Part1.A+, Load_Cell1.wire2
  N15: Part1.A-, Load_Cell1.wire4
  N16: Nokia_5110_LCD_Module1.RST, R1.Pin_0
  N17: R3.Pin_1, LED2.anode

notes:
  This is a simplified schematic. Missing:
  - soft latching circuit
  - main switch
  - auto backlight LDR circuit

custom parts:
  Load Cell - Red/white/black/green: A rectangle load cell/weighting pressure Sensor with four wires - Red, white, black, green. Normally corresponding with E+, E-, A+, A- respectively.
  : Nokia 5110 LCD with 8 pin. It's a 45mm*45mm module part. Description: The Nokia 5110 is a basic graphic LCD screen for lots of applications. It was originally intended for as a cell phone screen. This one is mounted on an easy to solder PCB. It uses the PCD8544 controller. The PCD8544 is a low power CMOS LCD controller/driver, designed to drive a graphic display of 48 rows and 84 columns. All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
